// Logisim project Gioco dell'oca_Progetto.circ as structural Verilog: 17 circuits, main circuit Gioco dell'oca
module Gioco_dell_oca (
);

  wire _0a, _0b, _1a, _1b, _2a, _2b, _3a, _3b, _4a, _4b, _5a, _5b, _6a, _6b, _7a, _7b, _8a, _8b, _9a, _9b,
       _10a, _10b, _11a, _11b, _12a, _12b, _13a, _13b, _14a, _14b, _15a, _15b, _16a, _16b, _17a, _17b, _18a,
       _18b, _19a, _19b, _20a, _20b, _21a, _21b, _22a, _22b, _23a, _23b, _24a, _24b, _25a, _25b, _26a, _26b,
       _27a, _27b, _28a, _28b, _29a, _29b, _30a, _30b, _31a, _31b, _32a, _32b, _33a, _33b, _34a, _34b, _35a,
       _35b, _36a, _36b, _37a, _37b, _38a, _38b, _39a, _39b, _40a, _40b, _41a, _41b, _42a, _42b, _43a, _43b,
       _44a, _44b, _45a, _45b, _46a, _46b, _47a, _47b, _48a, _48b, _49a, _49b, _50a, _50b, _51a, _51b, _52a,
       _52b, _53a, _53b, _54a, _54b, _55a, _55b, _56a, _56b, _57a, _57b, _58a, _58b, _59a, _59b, _60a, _60b,
       _61a, _61b, _62a, _62b, _63a, _63b, and_1_out, and_2_out, and_3_out, and_4_out, and_5_out, and_6_out,
       and_7_out, and_8_out, Bonus, Cambio, Clk, ClkDado, clock_1_out, comparator_1_eq, comparator_2_eq,
       Doppio, Fine, Fine2, First, On_Off, or_1_out, or_2_out, or_3_out, or_4_out, or_5_out, or_7_out,
       or_8_out, Pass, Sgn, Start, Stop, Tira, Tirato, Turno, Win;
  wire [1:0] counter_1_q, counter_3_q;
  wire [3:0] Dado1, Dado2, Dec1, Dec2, m0, m1, s0, s1, Uni1, Uni2;
  wire [4:0] Win1, Win2;
  wire [5:0] FinalPos1, FinalPos2, Pos1, Pos2, Somma;
  wire [6:0] Colore;
  wire [7:1] counter_2_q;

  LED led_1 (.in(_0a));
  LED led_2 (.in(_0b));
  Clock clock_1 (.out(clock_1_out));
  or or_1 (or_1_out, and_2_out, and_3_out);
  LED led_3 (.in(_33b));
  LED led_4 (.in(_33a));
  LED led_5 (.in(_34b));
  LED led_6 (.in(_35b));
  LED led_7 (.in(_36b));
  LED led_8 (.in(_37b));
  LED led_9 (.in(_38b));
  LED led_10 (.in(_39b));
  LED led_11 (.in(_1a));
  LED led_12 (.in(_1b));
  Counter #(.width(2), .max('h3)) counter_1 (
    .Q(counter_1_q), .clk(and_1_out), .clr(comparator_1_eq));  // open: load, D, count, carry
  and and_1 (and_1_out, Clk, Tirato);
  Counter #(.width(9), .max('h1ff)) counter_2 (
    .Q({Clk, counter_2_q, ClkDado}), .clk(clock_1_out));  // open: load, D, count, carry, clr
  and and_2 (and_2_out, Clk, ~Win);  // AND_Gate
  and and_3 (and_3_out, Clk, ~On_Off);  // AND_Gate
  timer timer_1 (.Clk(or_1_out), .On(On_Off), .m1(m1), .s1(s1), .m0(m0), .s0(s0));
  LED led_13 (.in(_32b));
  LED led_14 (.in(_32a));
  LED led_15 (.in(_34a));
  LED led_16 (.in(_35a));
  LED led_17 (.in(_36a));
  LED led_18 (.in(_37a));
  LED led_19 (.in(_38a));
  LED led_20 (.in(_40a));
  LED led_21 (.in(_39a));
  LED led_22 (.in(_40b));
  LED led_23 (.in(_2a));
  LED led_24 (.in(_2b));
  or or_2 (or_2_out, Stop, Fine);
  Comparator #(.width(2), .mode("unsigned")) comparator_1 (
    .a(counter_1_q), .b(2'b10), .eq(comparator_1_eq));  // open: gt, lt
  LED led_25 (.in(_31b));
  LED led_26 (.in(_31a));
  LED led_27 (.in(_61b));
  LED led_28 (.in(_61a));
  LED led_29 (.in(_62b));
  LED led_30 (.in(_63b));
  DotMatrix #(.matrixcols(3), .matrixrows(5)) dotmatrix_1 (.col0(Win1), .col1(Win1), .col2(Win1));
  DotMatrix #(.matrixcols(3), .matrixrows(5)) dotmatrix_2 (.col0(Win2), .col1(Win2), .col2(Win2));
  LED led_31 (.in(_41a));
  LED led_32 (.in(_41b));
  LED led_33 (.in(_3a));
  LED led_34 (.in(_3b));
  movimento movimento_1 (
    .Tiro(Somma), .Reset(or_2_out), ._0(_0a), ._1(_1a), ._2(_2a), ._3(_3a), ._4(_4a), ._5(_5a), ._6(_6a),
    ._7(_7a), ._8(_8a), ._9(_9a), ._10(_10a), ._11(_11a), ._12(_12a), ._13(_13a), ._14(_14a), ._15(_15a),
    ._16(_16a), ._17(_17a), ._18(_18a), ._19(_19a), ._20(_20a), ._21(_21a), ._22(_22a), ._23(_23a),
    ._24(_24a), ._25(_25a), ._26(_26a), ._27(_27a), ._28(_28a), ._29(_29a), ._30(_30a), ._31(_31a),
    ._32(_32a), ._33(_33a), ._34(_34a), ._35(_35a), ._36(_36a), ._37(_37a), ._38(_38a), ._39(_39a),
    ._40(_40a), ._41(_41a), ._42(_42a), ._43(_43a), ._44(_44a), ._45(_45a), ._46(_46a), ._47(_47a),
    ._48(_48a), ._49(_49a), ._50(_50a), ._51(_51a), ._52(_52a), ._53(_53a), ._54(_54a), ._55(_55a),
    ._56(_56a), ._57(_57a), ._58(_58a), ._59(_59a), ._60(_60a), ._61(_61a), ._62(_62a), ._63(_63a),
    .Lancia(or_3_out), .Pos(Pos1), .On(On_Off), .in_3(Sgn), .Clk(Clk), .Set(and_4_out), .Fine(Fine));
  and and_4 (and_4_out, Turno, comparator_1_eq);
  or or_3 (or_3_out, Pass, Stop);
  LED led_35 (.in(_30b));
  LED led_36 (.in(_30a));
  LED led_37 (.in(_60b));
  LED led_38 (.in(_60a));
  LED led_39 (.in(_62a));
  LED led_40 (.in(_63a));
  LED led_41 (.in(_42a));
  LED led_42 (.in(_42b));
  LED led_43 (.in(_4a));
  LED led_44 (.in(_4b));
  set_reset_1_bit set_reset_1_bit_1 (.Reset(Stop), .Set(Start), .Set_Reset(On_Off));
  LED led_45 (.in(_29b));
  LED led_46 (.in(_29a));
  LED led_47 (.in(_59b));
  LED led_48 (.in(_59a));
  Hex_Digit_Display hex_digit_display_1 (.value(Dado1));  // open: dp
  Hex_Digit_Display hex_digit_display_2 (.value(Dado2));  // open: dp
  DotMatrix dotmatrix_3 (.col0(Colore), .col1(Colore), .col2(Colore), .col3(Colore), .col4(Colore));
  LED led_49 (.in(_43a));
  LED led_50 (.in(_43b));
  LED led_51 (.in(_5a));
  LED led_52 (.in(_5b));
  check_bonus check_bonus_1 (
    .On_Off(On_Off), .ClkDado(ClkDado), .Pos1(Pos1), .Pos2(Pos2), .Somma(Somma), .Colore(Colore),
    .Tirato(Tirato), .Stop(Stop), .FinalPos1(FinalPos1), .FinalPos2(FinalPos2));
  LED led_53 (.in(_28b));
  LED led_54 (.in(_28a));
  LED led_55 (.in(_58b));
  LED led_56 (.in(_58a));
  Hex_Digit_Display hex_digit_display_3 (.value(m1));  // open: dp
  Button button_1 (.out(Tira));
  LED led_57 (.in(_44a));
  LED led_58 (.in(_44b));
  LED led_59 (.in(_6a));
  LED led_60 (.in(_6b));
  bin_to_dec bin_to_dec_1 (.Numero(Pos1), .Decina(Dec1), .Unita(Uni1));
  bonus bonus_1 (
    .Clk(Clk), .Cambio(Cambio), .Pos1(FinalPos1), .Pos2(FinalPos2), .On_Off(On_Off), .Bonus(Bonus), .Sgn(Sgn));
  LED led_61 (.in(_27b));
  LED led_62 (.in(_27a));
  LED led_63 (.in(_57b));
  LED led_64 (.in(_57a));
  Hex_Digit_Display hex_digit_display_4 (.value(s1));  // open: dp
  Hex_Digit_Display hex_digit_display_5 (.value(m0));  // open: dp
  Button button_2 (.out(Start));
  LED led_65 (.in(_45a));
  LED led_66 (.in(_45b));
  LED led_67 (.in(_7a));
  LED led_68 (.in(_7b));
  and and_5 (and_5_out, Clk, Tirato);
  LED led_69 (.in(_26b));
  LED led_70 (.in(_26a));
  LED led_71 (.in(_56b));
  LED led_72 (.in(_56a));
  Hex_Digit_Display hex_digit_display_6 (.value(s0));  // open: dp
  Button button_3 (.out(Stop));
  LED led_73 (.in(_46a));
  LED led_74 (.in(_46b));
  LED led_75 (.in(_8a));
  LED led_76 (.in(_8b));
  or or_4 (or_4_out, Stop, Fine2);
  Counter #(.width(2), .max('h3)) counter_3 (
    .Q(counter_3_q), .clk(and_5_out), .clr(comparator_2_eq));  // open: load, D, count, carry
  Comparator #(.width(2), .mode("unsigned")) comparator_2 (
    .a(counter_3_q), .b(2'b10), .eq(comparator_2_eq));  // open: gt, lt
  bin_to_dec bin_to_dec_2 (.Numero(Pos2), .Decina(Dec2), .Unita(Uni2));
  LED led_77 (.in(_25b));
  LED led_78 (.in(_25a));
  LED led_79 (.in(_55b));
  LED led_80 (.in(_55a));
  Hex_Digit_Display hex_digit_display_7 (.value(Dec1));  // open: dp
  Hex_Digit_Display hex_digit_display_8 (.value(Dec2));  // open: dp
  LED led_81 (.in(_47a));
  LED led_82 (.in(_47b));
  LED led_83 (.in(_9a));
  LED led_84 (.in(_9b));
  and and_6 (and_6_out, ~Turno, comparator_2_eq);  // AND_Gate
  or or_5 (or_5_out, Pass, Stop);
  LED led_85 (.in(_24b));
  LED led_86 (.in(_24a));
  LED led_87 (.in(_54b));
  LED led_88 (.in(_54a));
  Hex_Digit_Display hex_digit_display_9 (.value(Uni1));  // open: dp
  Hex_Digit_Display hex_digit_display_10 (.value(Uni2));  // open: dp
  LED led_89 (.in(_48a));
  LED led_90 (.in(_48b));
  LED led_91 (.in(_10a));
  LED led_92 (.in(_10b));
  movimento movimento_2 (
    .Tiro(Somma), .Reset(or_4_out), ._0(_0b), ._1(_1b), ._2(_2b), ._3(_3b), ._4(_4b), ._5(_5b), ._6(_6b),
    ._7(_7b), ._8(_8b), ._9(_9b), ._10(_10b), ._11(_11b), ._12(_12b), ._13(_13b), ._14(_14b), ._15(_15b),
    ._16(_16b), ._17(_17b), ._18(_18b), ._19(_19b), ._20(_20b), ._21(_21b), ._22(_22b), ._23(_23b),
    ._24(_24b), ._25(_25b), ._26(_26b), ._27(_27b), ._28(_28b), ._29(_29b), ._30(_30b), ._31(_31b),
    ._32(_32b), ._33(_33b), ._34(_34b), ._35(_35b), ._36(_36b), ._37(_37b), ._38(_38b), ._39(_39b),
    ._40(_40b), ._41(_41b), ._42(_42b), ._43(_43b), ._44(_44b), ._45(_45b), ._46(_46b), ._47(_47b),
    ._48(_48b), ._49(_49b), ._50(_50b), ._51(_51b), ._52(_52b), ._53(_53b), ._54(_54b), ._55(_55b),
    ._56(_56b), ._57(_57b), ._58(_58b), ._59(_59b), ._60(_60b), ._61(_61b), ._62(_62b), ._63(_63b),
    .Lancia(or_5_out), .Pos(Pos2), .On(On_Off), .in_3(Sgn), .Clk(Clk), .Set(and_6_out), .Fine(Fine2));
  and and_7 (and_7_out, ~First, On_Off);  // AND_Gate
  or or_6 (Cambio, Fine, Fine2);
  cambio_turno cambio_turno_1 (
    .Win(Win), .Cambio(Cambio), .Tira(Tira), .On_Off(On_Off), .Doppio(Doppio), .First(First), .Bonus(Bonus),
    .Stop(Stop), .Turno(Turno), .Pass(Pass));
  colore colore_1 (.Doppio(Doppio), .Cambio(Cambio), .Bonus(Bonus), .On_Off(On_Off), .Win(Win), .Colore(Colore));
  LED led_93 (.in(_23b));
  LED led_94 (.in(_23a));
  LED led_95 (.in(_53a));
  LED led_96 (.in(_52a));
  LED led_97 (.in(_51a));
  LED led_98 (.in(_50a));
  LED led_99 (.in(_49a));
  LED led_100 (.in(_49b));
  LED led_101 (.in(_11a));
  LED led_102 (.in(_11b));
  and and_8 (and_8_out, Clk, Cambio);
  LED led_103 (.in(_22b));
  LED led_104 (.in(_22a));
  LED led_105 (.in(_53b));
  LED led_106 (.in(_52b));
  LED led_107 (.in(_51b));
  LED led_108 (.in(_50b));
  LED led_109 (.in(_12a));
  LED led_110 (.in(_12b));
  vincitore vincitore_1 (
    .FinalPos1(FinalPos1), .FinalPos2(FinalPos2), .On_Off(and_7_out), .Clk(and_8_out), .Win(Win),
    .Win1(Win1), .Win2(Win2));
  LED led_111 (.in(_21a));
  LED led_112 (.in(_20a));
  LED led_113 (.in(_19a));
  LED led_114 (.in(_18a));
  LED led_115 (.in(_17a));
  LED led_116 (.in(_16a));
  LED led_117 (.in(_15a));
  LED led_118 (.in(_14a));
  LED led_119 (.in(_13a));
  LED led_120 (.in(_13b));
  or or_7 (or_7_out, Stop, Tirato);
  LED led_121 (.in(_21b));
  LED led_122 (.in(_20b));
  LED led_123 (.in(_19b));
  LED led_124 (.in(_18b));
  LED led_125 (.in(_17b));
  LED led_126 (.in(_16b));
  LED led_127 (.in(_15b));
  LED led_128 (.in(_14b));
  lancia_dadi lancia_dadi_1 (
    .On(Pass), .Lancia(Pass), .Clk(Clk), .ClkDado(ClkDado), .Dado1(Dado1), .Dado2(Dado2), .Off(or_7_out),
    .Stop(Stop), .Tirato(Tirato));
  or or_8 (or_8_out, Stop, Tira);
  set_reset_1_bit set_reset_1_bit_2 (.Reset(or_8_out), .Set(Start), .Set_Reset(First));
  somma_dadi somma_dadi_1 (.Dado1(Dado1), .Dado2(Dado2), .SommaDadi(Somma));
  Comparator #(.width(4), .mode("unsigned")) comparator_3 (.a(Dado1), .b(Dado2), .eq(Doppio));  // open: gt, lt

  // Notes on the sheet:
  //   Ritira i dadi
  //   ma torni indietro
  //   CLOCK
  //   TIMER
  //   Ritira i dadi
  //   GIOCATORE 1
  //   ON/OFF
  //   GESTIONE BONUS
  //   Attiva Bonus
  //   Check Bonus
  //   Da Capo
  //   Ritira i dadi
  //   GIOCO DELL'OCA
  //   POSIZIONE LED
  //   GIOCATORE 2
  //   Cambio Turno
  //   Colore Turno
  //   (si consiglia una frequenza di 1KHz)
  //   GESTIONE TURNO
  //   Ritira i dadi
  //   ma torni indietro
  //   VINCITORE
  //   Ritira i dadi
  //   ma torni indietro
  //   Ritira i dadi
  //   1. Si tirano a turno i dadi
  //   2. Si attende il proprio turno
  //   3. Nel caso di tiro doppio si tirano di nuovo i dadi
  //   GESTIONE DADI
  //   Lancia
  //   Primo Tiro
  //   Somma Dadi
  //   Tiro Doppio
  //   REGOLE DI GIOCO
  //   4. Nell'eventualità di finire su una casellaspeciale leggere le indicazioni
endmodule

module flip_flop_6_bit (
  input  [5:0] \input ,
  input  Clk,
  input  Write,
  output [5:0] \output 
);

  wire and_1_out;

  and and_1 (and_1_out, Clk, Write);
  D_Flip_Flop d_ff_1 (.clk(and_1_out), .D(\input [0]), .Q(\output [0]));  // open: Qn, preset, en, reset
  D_Flip_Flop d_ff_2 (.clk(and_1_out), .D(\input [1]), .Q(\output [1]));  // open: Qn, preset, en, reset
  D_Flip_Flop d_ff_3 (.clk(and_1_out), .D(\input [2]), .Q(\output [2]));  // open: Qn, preset, en, reset
  D_Flip_Flop d_ff_4 (.clk(and_1_out), .D(\input [3]), .Q(\output [3]));  // open: Qn, preset, en, reset
  D_Flip_Flop d_ff_5 (.clk(and_1_out), .D(\input [4]), .Q(\output [4]));  // open: Qn, preset, en, reset
  D_Flip_Flop d_ff_6 (.clk(and_1_out), .D(\input [5]), .Q(\output [5]));  // open: Qn, preset, en, reset
endmodule

module set_reset (
  input  [5:0] Input,
  input  Clk,
  input  Reset,
  input  Set,
  output [5:0] Output
);

  wire or_1_out;
  wire [5:0] and_1_out;
  wire [5:5] not_1_out;

  not not_1 (not_1_out[5], Reset);
  assign and_1_out = Input & {6{not_1_out[5]}};  // AND_Gate and_1, 6 bits wide
  or or_1 (or_1_out, Reset, Set);
  flip_flop_6_bit flip_flop_6_bit_1 (.\input (and_1_out), .Clk(Clk), .Write(or_1_out), .\output (Output));
endmodule

module dado (
  input  Clear,
  input  On,
  input  [2:0] Dado,
  input  ClkDado,
  output [3:0] dado_2
);

  wire and_1_out, comparator_1_gt, comparator_2_lt;
  wire [3:0] bit_extender_1_out, multiplexer_1_out;

  assign bit_extender_1_out = {{1{1'b0}}, Dado};  // Bit_Extender bit_extender_1
  Register #(.width(4)) register_1 (.D(multiplexer_1_out), .Q(dado_2), .clk(ClkDado), .clr(Clear));  // open: en
  Multiplexer #(.width(4)) multiplexer_1 (
    .in1(bit_extender_1_out), .out(multiplexer_1_out), .sel(and_1_out), .en(On));  // open: in0
  Comparator #(.width(4)) comparator_1 (.a(bit_extender_1_out), .b(4'b0000), .gt(comparator_1_gt));  // open: eq, lt
  Comparator #(.width(4)) comparator_2 (.a(bit_extender_1_out), .b(4'b0111), .lt(comparator_2_lt));  // open: gt, eq
  Hex_Digit_Display hex_digit_display_1 (.value(dado_2));  // open: dp
  and and_1 (and_1_out, comparator_1_gt, comparator_2_lt);

  // Other names for the same wires on the sheet: Dado_t[3:0] = dado_2; N[2:0] = Dado
endmodule

module lancia_dado (
  input  Tirato,
  input  Clk,
  output Tira
);

  wire and_1_out, d_ff_1_q;
  wire [3:0] counter_1_q;

  D_Flip_Flop d_ff_1 (.clk(Tirato), .D(1'b1), .Q(d_ff_1_q), .preset(1'b1), .reset(Tirato));  // open: Qn, en
  Counter #(.width(4), .max('hf), .ongoal("continue")) counter_1 (
    .Q(counter_1_q), .clk(and_1_out), .clr(Tirato));  // open: load, D, count, carry
  and and_1 (and_1_out, Clk, d_ff_1_q, ~Tira);  // AND_Gate
  Comparator #(.width(4), .mode("unsigned")) comparator_1 (.a(counter_1_q), .b(4'b0010), .eq(Tira));  // open: gt, lt
endmodule

module lancia_dadi (
  input  Stop,
  input  Off,
  input  On,
  input  Lancia,
  input  Clk,
  input  ClkDado,
  output [3:0] Dado1,
  output [3:0] Dado2,
  output Tirato
);

  wire and_1_out, On_t, Tirato_t;
  wire [2:0] N1, N2;

  and and_1 (and_1_out, ClkDado, ~Tirato_t);  // AND_Gate
  set_reset_1_bit set_reset_1_bit_1 (.Reset(Off), .Set(On), .Set_Reset(On_t));
  D_Flip_Flop d_ff_1 (.clk(Clk), .D(On_t), .Q(Tirato));  // open: Qn, preset, en, reset
  Random #(.width(3)) random_1 (.clk(and_1_out), .out(N1));  // open: next, clr
  Random #(.width(3), .seed(1)) random_2 (.clk(and_1_out), .out(N2));  // open: next, clr
  dado dado_1 (.Clear(Stop), .On(On_t), .Dado(N1), .ClkDado(ClkDado), .dado_2(Dado1));
  dado dado_2 (.Clear(Stop), .On(On_t), .Dado(N2), .ClkDado(ClkDado), .dado_2(Dado2));
  lancia_dado lancia_dado_1 (.Tirato(Lancia), .Clk(Clk), .Tira(Tirato_t));

  // Notes on the sheet:
  //   Per primo tiro
endmodule

module set_reset_1_bit (
  input  Reset,
  input  Set,
  output Set_Reset
);

  wire and_1_out, and_2_out, and_3_out, and_4_out;

  and and_1 (and_1_out, ~Reset, ~Set);  // AND_Gate
  and and_2 (and_2_out, ~Reset, Set);  // AND_Gate
  and and_3 (and_3_out, Set_Reset, and_1_out);
  and and_4 (and_4_out, 1'b1, and_2_out);
  or or_1 (Set_Reset, and_3_out, and_4_out);
endmodule

module timer (
  input  Clk,
  input  On,
  output [3:0] m1,
  output [3:0] s1,
  output [3:0] m0,
  output [3:0] s0
);

  wire and_1_out, and_3_out, and_4_out, and_5_out, and_6_out, Avanti, or_1_out, or_2_out, or_3_out, or_4_out;

  Counter #(.width(4), .max('hf)) counter_1 (.Q(s0), .clk(and_1_out), .clr(or_1_out));  // open: load, D, count, carry
  and and_1 (and_1_out, Clk, On);
  or or_1 (or_1_out, and_3_out, Avanti);
  and and_2 (Avanti, ~On, Clk);  // AND_Gate
  and and_3 (and_3_out, ~s0[0], s0[1], ~s0[2], s0[3]);  // AND_Gate
  Counter #(.width(4), .max('hf)) counter_2 (.Q(s1), .clk(or_1_out), .clr(or_2_out));  // open: load, D, count, carry
  or or_2 (or_2_out, and_4_out, Avanti);
  and and_4 (and_4_out, ~s1[0], s1[1], s1[2], ~s1[3]);  // AND_Gate
  Counter #(.width(4), .max('hf)) counter_3 (.Q(m0), .clk(or_2_out), .clr(or_3_out));  // open: load, D, count, carry
  or or_3 (or_3_out, and_5_out, Avanti);
  and and_5 (and_5_out, ~m0[0], m0[1], ~m0[2], m0[3]);  // AND_Gate
  Counter #(.width(4), .max('hf)) counter_4 (.Q(m1), .clk(or_3_out), .clr(or_4_out));  // open: load, D, count, carry
  or or_4 (or_4_out, and_6_out, Avanti);
  and and_6 (and_6_out, ~m1[0], m1[1], m1[2], ~m1[3]);  // AND_Gate
endmodule

module movimento (
  input  Lancia,
  input  On,
  input  in_3,
  input  Clk,
  input  [5:0] Tiro,
  input  Reset,
  input  Set,
  output _0,
  output _1,
  output _2,
  output _3,
  output _4,
  output _5,
  output _6,
  output _7,
  output _8,
  output _9,
  output _10,
  output _11,
  output _12,
  output _13,
  output _14,
  output _15,
  output _16,
  output _17,
  output _18,
  output _19,
  output _20,
  output _21,
  output _22,
  output _23,
  output _24,
  output _25,
  output _26,
  output _27,
  output _28,
  output _29,
  output _30,
  output _31,
  output _32,
  output _33,
  output _34,
  output _35,
  output _36,
  output _37,
  output _38,
  output _39,
  output _40,
  output _41,
  output _42,
  output _43,
  output _44,
  output _45,
  output _46,
  output _47,
  output _48,
  output _49,
  output _50,
  output _51,
  output _52,
  output _53,
  output _54,
  output _55,
  output _56,
  output _57,
  output _58,
  output _59,
  output _60,
  output _61,
  output _62,
  output _63,
  output Fine,
  output [5:0] Pos
);

  wire adder_2_cout, adder_3_out, and_1_out, and_2_out, and_3_out, and_4_out, and_5_out, and_6_out,
       and_8_out, and_9_out, comparator_1_eq, comparator_2_eq, Count, DaCapo, decoder_1_out0, decoder_1_out1,
       not_1_out, On_t, or_1_out, or_2_out, set_reset_1_bit_2_set_reset, Set_t, subtractor_1_bout;
  wire [1:0] counter_2_q;
  wire [5:0] adder_2_out, counter_1_q, Ris, subtractor_1_out;

  Decoder decoder_1 (.out0(decoder_1_out0), .out1(decoder_1_out1), .sel(Pos[5]), .en(On_t));
  set_reset_1_bit set_reset_1_bit_1 (.Reset(Reset), .Set(Set), .Set_Reset(Set_t));
  Decoder #(.select(5)) decoder_2 (
    .out0(_0), .out1(_1), .out2(_2), .out3(_3), .out4(_4), .out5(_5), .out6(_6), .out7(_7), .out8(_8),
    .out9(_9), .out10(_10), .out11(_11), .out12(_12), .out13(_13), .out14(_14), .out15(_15), .out16(_16),
    .out17(_17), .out18(_18), .out19(_19), .out20(_20), .out21(_21), .out22(_22), .out23(_23), .out24(_24),
    .out25(_25), .out26(_26), .out27(_27), .out28(_28), .out29(_29), .out30(_30), .out31(_31),
    .sel(Pos[4:0]), .en(and_1_out));
  and and_1 (and_1_out, ~Pos[5], decoder_1_out0);  // AND_Gate
  and and_2 (and_2_out, decoder_1_out1, Pos[5]);
  Decoder #(.select(5)) decoder_3 (
    .out0(_32), .out1(_33), .out2(_34), .out3(_35), .out4(_36), .out5(_37), .out6(_38), .out7(_39),
    .out8(_40), .out9(_41), .out10(_42), .out11(_43), .out12(_44), .out13(_45), .out14(_46), .out15(_47),
    .out16(_48), .out17(_49), .out18(_50), .out19(_51), .out20(_52), .out21(_53), .out22(_54), .out23(_55),
    .out24(_56), .out25(_57), .out26(_58), .out27(_59), .out28(_60), .out29(_61), .out30(_62), .out31(_63),
    .sel(Pos[4:0]), .en(and_2_out));
  Comparator #(.width(6), .mode("unsigned")) comparator_1 (
    .a(Tiro), .b({6{1'b0}}), .eq(comparator_1_eq));  // open: gt, lt
  Adder #(.width(1)) adder_1 (.a(Count), .b(comparator_1_eq), .out(Fine));  // open: cin, cout
  and and_3 (and_3_out, On_t, Clk, ~Count);  // AND_Gate
  and and_4 (and_4_out, ~On_t, Clk);  // AND_Gate
  Comparator #(.width(6), .mode("unsigned")) comparator_2 (
    .a(Pos), .b(6'b111010), .eq(comparator_2_eq));  // open: gt, lt
  Adder #(.width(6)) adder_2 (.a(Pos), .b(6'b000001), .out(adder_2_out), .cout(adder_2_cout));  // open: cin
  Subtractor #(.width(6)) subtractor_1 (
    .a(Pos), .b(6'b000001), .out(subtractor_1_out), .bout(subtractor_1_bout));  // open: bin
  Counter #(.width(6), .max('h3f)) counter_1 (
    .Q(counter_1_q), .clk(and_5_out), .clr(Lancia));  // open: load, D, count, carry
  and and_5 (and_5_out, Clk, Set_t, ~Count);  // AND_Gate
  or or_1 (or_1_out, ~Set_t, subtractor_1_bout);  // OR_Gate
  Comparator #(.width(6), .mode("unsigned")) comparator_3 (.a(counter_1_q), .b(Tiro), .eq(Count));  // open: gt, lt
  or or_2 (or_2_out, and_3_out, and_4_out);
  not not_1 (not_1_out, On_t);
  and and_6 (and_6_out, comparator_2_eq, Fine);
  and and_7 (On_t, ~DaCapo, On);  // AND_Gate
  Adder #(.width(1)) adder_3 (.a(in_3), .b(set_reset_1_bit_2_set_reset), .out(adder_3_out));  // open: cin, cout
  set_reset_1_bit set_reset_1_bit_2 (.Reset(or_1_out), .Set(adder_2_cout), .Set_Reset(set_reset_1_bit_2_set_reset));
  set_reset set_reset_1 (.Input(Ris), .Clk(or_2_out), .Reset(not_1_out), .Set(Set_t), .Output(Pos));
  and and_8 (and_8_out, and_9_out, Clk);
  and and_9 (and_9_out, and_6_out, Clk);
  Multiplexer #(.width(6)) multiplexer_1 (
    .in0(adder_2_out), .in1(subtractor_1_out), .out(Ris), .sel(adder_3_out), .en(On_t));
  Counter #(.width(2), .max('h3)) counter_2 (
    .Q(counter_2_q), .clk(and_8_out), .clr(DaCapo));  // open: load, D, count, carry
  Comparator #(.width(2), .mode("unsigned")) comparator_4 (.a(counter_2_q), .b(2'b10), .eq(DaCapo));  // open: gt, lt

  // Other names for the same wires on the sheet: Accendi = On; Dadi[5:0] = Tiro; Num[4:0] = Pos[4:0]; _2nd = Pos[5];
  //   tunnel = in_3
endmodule

module somma_dadi (
  input  [3:0] Dado1,
  input  [3:0] Dado2,
  output [5:0] SommaDadi
);

  wire [3:0] adder_1_out;

  assign SommaDadi = {{2{1'b0}}, adder_1_out};  // Bit_Extender bit_extender_1
  Adder #(.width(4)) adder_1 (.a(Dado1), .b(Dado2), .out(adder_1_out));  // open: cin, cout
endmodule

module bin_to_dec (
  input  [5:0] Numero,
  output [3:0] Unita,
  output [3:0] Decina
);

  wire [5:0] divider_1_out, divider_1_rem;

  Divider #(.width(6)) divider_1 (.a(Numero), .b(6'b001010), .out(divider_1_out), .rem(divider_1_rem));  // open: upper
  Hex_Digit_Display hex_digit_display_1 (.value(Decina));  // open: dp
  Bit_Extender #(.in_width(6), .out_width(4)) bit_extender_1 (.in(divider_1_out), .out(Decina));
  Hex_Digit_Display hex_digit_display_2 (.value(Unita));  // open: dp
  Bit_Extender #(.in_width(6), .out_width(4)) bit_extender_2 (.in(divider_1_rem), .out(Unita));
endmodule

module bonus (
  input  Clk,
  input  Cambio,
  input  [5:0] Pos1,
  input  [5:0] Pos2,
  input  On_Off,
  output Bonus,
  output Sgn
);

  wire and_1_out, comparator_1_eq, comparator_2_eq, comparator_3_eq, comparator_4_eq, comparator_5_eq,
       comparator_6_eq, comparator_7_eq, comparator_8_eq, comparator_9_eq, comparator_10_eq,
       comparator_11_eq, comparator_12_eq, not_1_out, or_1_out, or_2_out, or_3_out, or_4_out, or_5_out,
       or_6_out, or_7_out, or_8_out;

  Comparator #(.width(6), .mode("unsigned")) comparator_1 (
    .a(6'b100001), .b(Pos1), .eq(comparator_1_eq));  // open: gt, lt
  Comparator #(.width(6), .mode("unsigned")) comparator_2 (
    .a(6'b100001), .b(Pos2), .eq(comparator_2_eq));  // open: gt, lt
  Comparator #(.width(6), .mode("unsigned")) comparator_3 (
    .a(6'b010101), .b(Pos1), .eq(comparator_3_eq));  // open: gt, lt
  Comparator #(.width(6), .mode("unsigned")) comparator_4 (
    .a(6'b010101), .b(Pos2), .eq(comparator_4_eq));  // open: gt, lt
  Comparator #(.width(6), .mode("unsigned")) comparator_5 (
    .a(6'b110011), .b(Pos1), .eq(comparator_5_eq));  // open: gt, lt
  Comparator #(.width(6), .mode("unsigned")) comparator_6 (
    .a(6'b110011), .b(Pos2), .eq(comparator_6_eq));  // open: gt, lt
  Comparator #(.width(6), .mode("unsigned")) comparator_7 (
    .a(6'b001101), .b(Pos1), .eq(comparator_7_eq));  // open: gt, lt
  Comparator #(.width(6), .mode("unsigned")) comparator_8 (
    .a(6'b001101), .b(Pos2), .eq(comparator_8_eq));  // open: gt, lt
  Comparator #(.width(6), .mode("unsigned")) comparator_9 (
    .a(6'b011011), .b(Pos1), .eq(comparator_9_eq));  // open: gt, lt
  Comparator #(.width(6), .mode("unsigned")) comparator_10 (
    .a(6'b011011), .b(Pos2), .eq(comparator_10_eq));  // open: gt, lt
  Comparator #(.width(6), .mode("unsigned")) comparator_11 (
    .a(6'b101001), .b(Pos1), .eq(comparator_11_eq));  // open: gt, lt
  Comparator #(.width(6), .mode("unsigned")) comparator_12 (
    .a(6'b101001), .b(Pos2), .eq(comparator_12_eq));  // open: gt, lt
  or or_1 (or_1_out, comparator_1_eq, comparator_2_eq);
  or or_2 (or_2_out, comparator_3_eq, comparator_4_eq);
  or or_3 (or_3_out, comparator_5_eq, comparator_6_eq);
  or or_4 (or_4_out, comparator_7_eq, comparator_8_eq);
  or or_5 (or_5_out, comparator_9_eq, comparator_10_eq);
  or or_6 (or_6_out, comparator_11_eq, comparator_12_eq);
  or or_7 (or_7_out, or_1_out, or_2_out, or_3_out);
  or or_8 (or_8_out, or_4_out, or_5_out, or_6_out);
  and and_1 (and_1_out, Clk, Cambio);
  D_Flip_Flop d_ff_1 (.clk(and_1_out), .D(or_7_out), .Q(Sgn), .en(On_Off), .reset(not_1_out));  // open: Qn, preset
  not not_1 (not_1_out, On_Off);
  or or_9 (Bonus, or_7_out, or_8_out);
endmodule

module colore (
  input  Doppio,
  input  Cambio,
  input  Bonus,
  input  On_Off,
  input  Win,
  output [6:0] Colore
);

  wire and_1_out, counter_1_q, not_2_out;

  Counter #(.width(1), .max('h1)) counter_1 (
    .Q(counter_1_q), .clk(and_1_out), .clr(not_2_out));  // open: load, D, count, carry
  not not_1 (Colore[6], counter_1_q);
  not not_2 (not_2_out, On_Off);
  and and_1 (and_1_out, ~Bonus, ~Doppio, Cambio, ~Win);  // AND_Gate

  assign Colore[5:0] = {6{Colore[6]}};
endmodule

module vincitore (
  input  [5:0] FinalPos1,
  input  [5:0] FinalPos2,
  input  On_Off,
  input  Clk,
  output Win,
  output [4:0] Win1,
  output [4:0] Win2
);

  wire comparator_1_eq, comparator_2_eq;

  Comparator #(.width(6), .mode("unsigned")) comparator_1 (
    .a(FinalPos1), .b({6{1'b1}}), .eq(comparator_1_eq));  // open: gt, lt
  or or_1 (Win, comparator_1_eq, comparator_2_eq);
  Comparator #(.width(6), .mode("unsigned")) comparator_2 (
    .a(FinalPos2), .b({6{1'b1}}), .eq(comparator_2_eq));  // open: gt, lt
  and and_1 (Win1[4], On_Off, Clk, comparator_1_eq);
  and and_2 (Win2[4], comparator_2_eq, Clk, On_Off);

  assign Win1[3:0] = {4{Win1[4]}};
  assign Win2[3:0] = {4{Win2[4]}};
endmodule

module fermo_turno (
  input  Clk,
  input  Turno,
  input  Cambio,
  input  [5:0] Pos1,
  input  [5:0] Pos2,
  input  On_Off,
  output StopTurno
);

  wire comparator_1_eq, comparator_2_eq;

  Comparator #(.width(6), .mode("unsigned")) comparator_1 (
    .a(6'b001111), .b(Pos1), .eq(comparator_1_eq));  // open: gt, lt
  Comparator #(.width(6), .mode("unsigned")) comparator_2 (
    .a(6'b001111), .b(Pos2), .eq(comparator_2_eq));  // open: gt, lt
  Counter #(.width(1), .max('h1)) counter_1 (.clk(StopTurno));  // open: load, D, count, Q, carry, clr
  or or_1 (StopTurno, comparator_1_eq, comparator_2_eq);

  // Notes on the sheet:
  //   15
  //   15
endmodule

module cambio_turno (
  input  Win,
  input  Cambio,
  input  Tira,
  input  On_Off,
  input  Doppio,
  input  First,
  input  Bonus,
  input  Stop,
  output Turno,
  output Pass
);

  wire and_1_out, and_2_out, and_3_out, and_4_out;

  and and_1 (and_1_out, ~Win, Cambio, Tira, On_Off);  // AND_Gate
  or or_1 (Pass, and_1_out, and_2_out);
  and and_2 (and_2_out, Tira, On_Off, First);
  Counter #(.width(1), .max('h1)) counter_1 (.Q(Turno), .clk(and_3_out), .clr(Stop));  // open: load, D, count, carry
  and and_3 (and_3_out, Pass, ~and_4_out, ~Bonus);  // AND_Gate
  and and_4 (and_4_out, Doppio, ~First);  // AND_Gate
endmodule

module check_bonus (
  input  On_Off,
  input  ClkDado,
  input  [5:0] Pos1,
  input  [5:0] Pos2,
  input  [5:0] Somma,
  input  [6:0] Colore,
  input  Tirato,
  input  Stop,
  output [5:0] FinalPos1,
  output [5:0] FinalPos2
);

  wire [5:0] adder_1_out, multiplexer_1_out, set_reset_1_output;

  Multiplexer #(.width(6)) multiplexer_1 (
    .in0(Pos2), .in1(Pos1), .out(multiplexer_1_out), .sel(Colore[6]), .en(On_Off));
  Adder #(.width(6)) adder_1 (.a(multiplexer_1_out), .b(Somma), .out(adder_1_out));  // open: cin, cout
  set_reset set_reset_1 (.Input(adder_1_out), .Clk(ClkDado), .Reset(Stop), .Set(Tirato), .Output(set_reset_1_output));
  Demultiplexer #(.width(6)) demultiplexer_1 (
    .out0(FinalPos2), .out1(FinalPos1), .in(set_reset_1_output), .sel(Colore[6]), .en(On_Off));

  // Other names for the same wires on the sheet: Giocatore = Colore[6]
endmodule
